# Fritzing sketch Alarm_Clock_Simon_Schematic_Stack (saved by Fritzing 0.8.5b)
circuit board: 9.5cm x 2.5cm
circuit board: 9.5cm x 2.5cm
breadboards: 3

parts:
  J1 = Piezo Speaker
  IC3 = IC, DIP package, 24 pins [chip_label=MAX2719]
  J7 = female pin header, 6 pins [form="♀ (female)"]
  J8 = female pin header, 6 pins [form="♀ (female)"]
  R7 = Resistor [tolerance=±5% resistance=220 package=THT]
  C6 = Ceramic Capacitor [capacitance=100nF package="100 mil [THT, multilayer]"]
  U5 = atmega328 [package=dip]
  C10 = Electrolytic Capacitor [capacitance=10µF package="100 mil [THT, electrolytic]"]
  XTAL3 = Crystal [frequency="16 Mhz" package=THT]
  C11 = Ceramic Capacitor [capacitance=100nF package="100 mil [THT, multilayer]"]
  C12 = Electrolytic Capacitor [capacitance=10µF package="100 mil [THT, electrolytic]"]
  C13 = Ceramic Capacitor [capacitance=100nF package="100 mil [THT, multilayer]"]
  U6 = Voltage Regulator - 5V [package="TO220 [THT]"]
  Batt_+ = female pin header, 1 pin [form="♀ (female)"]
  Batt_- = female pin header, 1 pin [form="♀ (female)"]
  J14 = female pin header, 4 pins [form="♀ (female)"]
  J13 = female pin header, 3 pins [form="♀ (female)"]
  J16 = female pin header, 2 pins [form="♀ (female)"]
  J18 = female pin header, 2 pins [form="♀ (female)"]
  J19 = female pin header, 2 pins [form="♀ (female)"]
  Speaker_-3 = female pin header, 1 pin [form="♀ (female)"]
  Spkr_+3 = female pin header, 1 pin [form="♀ (female)"]
  R8 = Resistor [tolerance=±5% resistance=220 package=THT]
  R9 = Resistor [tolerance=±5% resistance=220 package=THT]
  R10 = Resistor [tolerance=±5% resistance=220 package=THT]
  R11 = Resistor [tolerance=±5% resistance=220 package=THT]
  R12 = Resistor [tolerance=±5% resistance=220 package=THT]
  -_for_LEDs = female pin header, 1 pin [form="♀ (female)"]
  +_for_buttons = female pin header, 1 pin [form="♀ (female)"]
  R13 = Resistor [tolerance=±5% resistance=220 package=THT]
  R14 = Resistor [tolerance=±5% resistance=220 package=THT]
  R15 = Resistor [tolerance=±5% resistance=220 package=THT]
  J17 = female pin header, 2 pins [form="♀ (female)"]
  IC4 = DS1307 [package=THT]
  Xtal = female pin header, 1 pin [form="♀ (female)"]
  32_kHz = female pin header, 1 pin [form="♀ (female)"]
  J12 = female pin header, 4 pins [form="♀ (female)"]
  J9 = female pin header, 3 pins [form="♀ (female)"]

nets:
  GND: J1.pin1, IC3.pin4, C6.0, U5.GND, C10.-, C11.0, C12.-, C13.0, U6.GND, Batt_-.pin1, J14.pin2, Speaker_-3.pin1, R8.Pin_0, R9.Pin_0, R10.Pin_0, R11.Pin_0, R13.Pin_1, IC4.0V, J12.pin2
  N1: J1.pin2, Spkr_+3.pin1, R12.Pin_0
  N2: IC3.pin1, U5.D4, J13.pin1, J9.pin1
  N3: IC3.pin2, J7.pin6
  N4: IC3.pin6, J8.pin4
  N5: IC3.pin7, J8.pin1
  N6: IC3.pin11, J8.pin5
  N7: IC3.pin12, U5.D2, J13.pin3, J9.pin3
  N8: IC3.pin13, U5.D3_(PWM), J13.pin2, J9.pin2
  N9: IC3.pin14, J8.pin2
  N10: IC3.pin15, J8.pin3
  N11: IC3.pin16, J8.pin6
  N12: IC3.pin17, J7.pin5
  N13: IC3.pin18, R7.Pin_1
  N14: IC3.pin19, R7.Pin_0, C6.1, U5.VCC, U5.AVCC, U5.AREF, C10.+, U6.output_voltage, J14.pin1, +_for_buttons.pin1, R14.Pin_0, R15.Pin_0, IC4.+V, J12.pin1
  N15: IC3.pin20, J7.pin4
  N16: IC3.pin21, J7.pin1
  N17: IC3.pin22, J7.pin3
  N18: IC3.pin23, J7.pin2
  N19: U5.XLAT1, XTAL3.pin_0, C13.1
  N20: U5.XLAT2, XTAL3.pin_1, C11.1
  N21: U5.D5_(PWM), R12.Pin_1
  N22: U5.D6_(PWM), J16.pin1, R8.Pin_1
  N23: U5.D7, J16.pin2
  N24: U5.D8, R9.Pin_1, J17.pin1
  N25: U5.D9_(PWM), J17.pin2
  N26: U5.D10_(PWM), J18.pin2, R11.Pin_1
  N27: U5.D11_(PWM), J18.pin1
  N28: U5.D12, J19.pin2, R10.Pin_1
  N29: U5.D13, J19.pin1
  N30: U5.A4, J14.pin3, R15.Pin_1, IC4.SDA_-_I2C_Data, J12.pin3
  N31: U5.A5, J14.pin4, R14.Pin_1, IC4.SCL_-_I2C_Clock, J12.pin4
  N32: C12.+, U6.input_voltage
  N33: Batt_+.pin1, IC4.Vbat_-_Backup_Supply
  N34: -_for_LEDs.pin1, R13.Pin_0
  N35: IC4.X1_-_Crystal, 32_kHz.pin1
  N36: IC4.X2_-_Crystal, Xtal.pin1

notes:
  *
