# Fritzing sketch Alarm_Clock_Simon_Schematic_Stack_Production (saved by Fritzing 0.7.12b)
breadboards: 3

parts:
  IC3 = IC, DIP package, 24 pins [chip_label=MAX2719]
  J7 = female pin header, 6 pins [form="♀ (female)"]
  J8 = female pin header, 6 pins [form="♀ (female)"]
  R7 = Resistor [tolerance=±5% resistance=220 package=THT]
  C6 = Ceramic Capacitor [capacitance=100nF package="100 mil [THT, multilayer]"]
  U5 = atmega328 [package=dip]
  C10 = Electrolytic Capacitor [capacitance=10µF package="100 mil [THT, electrolytic]"]
  XTAL3 = Crystal [frequency="16 Mhz" package=THT]
  C11 = Ceramic Capacitor [capacitance=100nF package="100 mil [THT, multilayer]"]
  C12 = Electrolytic Capacitor [capacitance=10µF package="100 mil [THT, electrolytic]"]
  C13 = Ceramic Capacitor [capacitance=100nF package="100 mil [THT, multilayer]"]
  U6 = Voltage Regulator - 5V [package="TO220 [THT]"]
  IC4 = DS1307 [package=THT]
  Xtal = female pin header, 1 pin [form="♀ (female)"]
  32_kHz = female pin header, 1 pin [form="♀ (female)"]
  Batt_+ = female pin header, 1 pin [form="♀ (female)"]
  Batt_- = female pin header, 1 pin [form="♀ (female)"]
  J12 = female pin header, 4 pins [form="♀ (female)"]
  J14 = female pin header, 4 pins [form="♀ (female)"]
  J9 = female pin header, 3 pins [form="♀ (female)"]
  J13 = female pin header, 3 pins [form="♀ (female)"]
  J16 = female pin header, 2 pins [form="♀ (female)"]
  J18 = female pin header, 2 pins [form="♀ (female)"]
  J19 = female pin header, 2 pins [form="♀ (female)"]
  Speaker_-3 = female pin header, 1 pin [form="♀ (female)"]
  Spkr_+3 = female pin header, 1 pin [form="♀ (female)"]
  R8 = Resistor [tolerance=±5% resistance=220 package=THT]
  R9 = Resistor [tolerance=±5% resistance=220 package=THT]
  R10 = Resistor [tolerance=±5% resistance=220 package=THT]
  R11 = Resistor [tolerance=±5% resistance=220 package=THT]
  R12 = Resistor [tolerance=±5% resistance=220 package=THT]
  -_for_LEDs = female pin header, 1 pin [form="♀ (female)"]
  +_for_buttons = female pin header, 1 pin [form="♀ (female)"]
  R13 = Resistor [tolerance=±5% resistance=220 package=THT]
  R14 = Resistor [tolerance=±5% resistance=220 package=THT]
  R15 = Resistor [tolerance=±5% resistance=220 package=THT]
  J17 = female pin header, 2 pins [form="♀ (female)"]
  U7 = atmega328 [package=dip]
  IC5 = IC, DIP package, 24 pins [chip_label=MAX2719]
  C14 = Electrolytic Capacitor [capacitance=10µF package="100 mil [THT, electrolytic]"]
  XTAL4 = Crystal [frequency="16 Mhz" package=THT]
  J20 = female pin header, 6 pins [form="♀ (female)"]
  C15 = Ceramic Capacitor [capacitance=100nF package="100 mil [THT, multilayer]"]
  C16 = Electrolytic Capacitor [capacitance=10µF package="100 mil [THT, electrolytic]"]
  J21 = female pin header, 6 pins [form="♀ (female)"]
  C17 = Ceramic Capacitor [capacitance=100nF package="100 mil [THT, multilayer]"]
  R16 = Resistor [tolerance=±5% resistance=220 package=THT]
  R17 = Resistor [tolerance=±5% resistance=220 package=THT]
  R18 = Resistor [tolerance=±5% resistance=220 package=THT]
  R19 = Resistor [tolerance=±5% resistance=220 package=THT]
  R20 = Resistor [tolerance=±5% resistance=220 package=THT]
  R21 = Resistor [tolerance=±5% resistance=220 package=THT]
  R22 = Resistor [tolerance=±5% resistance=220 package=THT]
  R23 = Resistor [tolerance=±5% resistance=220 package=THT]
  R24 = Resistor [tolerance=±5% resistance=220 package=THT]
  U8 = Voltage Regulator - 5V [package="TO220 [THT]"]
  J22 = female pin header, 3 pins [form="♀ (female)"]
  J23 = female pin header, 3 pins [form="♀ (female)"]
  C18 = Ceramic Capacitor [capacitance=100nF package="100 mil [THT, multilayer]"]
  Speaker_-4 = female pin header, 1 pin [form="♀ (female)"]
  Spkr_+4 = female pin header, 1 pin [form="♀ (female)"]
  IC6 = DS1307 [package=THT]
  Batt_-1 = female pin header, 1 pin [form="♀ (female)"]
  Batt_+1 = female pin header, 1 pin [form="♀ (female)"]
  32_kHz1 = female pin header, 1 pin [form="♀ (female)"]
  Xtal1 = female pin header, 1 pin [form="♀ (female)"]
  J24 = female pin header, 4 pins [form="♀ (female)"]
  J25 = female pin header, 4 pins [form="♀ (female)"]
  J26 = female pin header, 2 pins [form="♀ (female)"]
  J27 = female pin header, 2 pins [form="♀ (female)"]
  J28 = female pin header, 2 pins [form="♀ (female)"]
  J29 = female pin header, 2 pins [form="♀ (female)"]
  +_for_buttons1 = female pin header, 1 pin [form="♀ (female)"]
  -_for_LEDs1 = female pin header, 1 pin [form="♀ (female)"]
  U9 = atmega328 [package=dip]
  U10 = atmega328 [package=dip]
  IC7 = IC, DIP package, 24 pins [chip_label=MAX2719]
  IC8 = IC, DIP package, 24 pins [chip_label=MAX2719]
  C19 = Electrolytic Capacitor [capacitance=10µF package="100 mil [THT, electrolytic]"]
  C20 = Electrolytic Capacitor [capacitance=10µF package="100 mil [THT, electrolytic]"]
  XTAL5 = Crystal [frequency="16 Mhz" package=THT]
  XTAL6 = Crystal [frequency="16 Mhz" package=THT]
  J30 = female pin header, 6 pins [form="♀ (female)"]
  J31 = female pin header, 6 pins [form="♀ (female)"]
  C21 = Ceramic Capacitor [capacitance=100nF package="100 mil [THT, multilayer]"]
  C22 = Ceramic Capacitor [capacitance=100nF package="100 mil [THT, multilayer]"]
  C23 = Electrolytic Capacitor [capacitance=10µF package="100 mil [THT, electrolytic]"]
  C24 = Electrolytic Capacitor [capacitance=10µF package="100 mil [THT, electrolytic]"]
  J32 = female pin header, 6 pins [form="♀ (female)"]
  J33 = female pin header, 6 pins [form="♀ (female)"]
  C25 = Ceramic Capacitor [capacitance=100nF package="100 mil [THT, multilayer]"]
  C26 = Ceramic Capacitor [capacitance=100nF package="100 mil [THT, multilayer]"]
  R25 = Resistor [tolerance=±5% resistance=220 package=THT]
  R26 = Resistor [tolerance=±5% resistance=220 package=THT]
  R27 = Resistor [tolerance=±5% resistance=220 package=THT]
  R28 = Resistor [tolerance=±5% resistance=220 package=THT]
  R29 = Resistor [tolerance=±5% resistance=220 package=THT]
  R30 = Resistor [tolerance=±5% resistance=220 package=THT]
  R31 = Resistor [tolerance=±5% resistance=220 package=THT]
  R32 = Resistor [tolerance=±5% resistance=220 package=THT]
  R33 = Resistor [tolerance=±5% resistance=220 package=THT]
  R34 = Resistor [tolerance=±5% resistance=220 package=THT]
  R35 = Resistor [tolerance=±5% resistance=220 package=THT]
  R36 = Resistor [tolerance=±5% resistance=220 package=THT]
  R37 = Resistor [tolerance=±5% resistance=220 package=THT]
  R38 = Resistor [tolerance=±5% resistance=220 package=THT]
  R39 = Resistor [tolerance=±5% resistance=220 package=THT]
  R40 = Resistor [tolerance=±5% resistance=220 package=THT]
  R41 = Resistor [tolerance=±5% resistance=220 package=THT]
  R42 = Resistor [tolerance=±5% resistance=220 package=THT]
  U11 = Voltage Regulator - 5V [package="TO220 [THT]"]
  U12 = Voltage Regulator - 5V [package="TO220 [THT]"]
  J34 = female pin header, 3 pins [form="♀ (female)"]
  J35 = female pin header, 3 pins [form="♀ (female)"]
  J36 = female pin header, 3 pins [form="♀ (female)"]
  J37 = female pin header, 3 pins [form="♀ (female)"]
  C27 = Ceramic Capacitor [capacitance=100nF package="100 mil [THT, multilayer]"]
  C28 = Ceramic Capacitor [capacitance=100nF package="100 mil [THT, multilayer]"]
  Speaker_-5 = female pin header, 1 pin [form="♀ (female)"]
  Speaker_-6 = female pin header, 1 pin [form="♀ (female)"]
  Spkr_+5 = female pin header, 1 pin [form="♀ (female)"]
  Spkr_+6 = female pin header, 1 pin [form="♀ (female)"]
  IC9 = DS1307 [package=THT]
  IC10 = DS1307 [package=THT]
  Batt_-2 = female pin header, 1 pin [form="♀ (female)"]
  Batt_-3 = female pin header, 1 pin [form="♀ (female)"]
  Batt_+2 = female pin header, 1 pin [form="♀ (female)"]
  Batt_+3 = female pin header, 1 pin [form="♀ (female)"]
  32_kHz2 = female pin header, 1 pin [form="♀ (female)"]
  32_kHz3 = female pin header, 1 pin [form="♀ (female)"]
  Xtal2 = female pin header, 1 pin [form="♀ (female)"]
  Xtal3 = female pin header, 1 pin [form="♀ (female)"]
  J38 = female pin header, 4 pins [form="♀ (female)"]
  J39 = female pin header, 4 pins [form="♀ (female)"]
  J40 = female pin header, 4 pins [form="♀ (female)"]
  J41 = female pin header, 4 pins [form="♀ (female)"]
  J42 = female pin header, 2 pins [form="♀ (female)"]
  J43 = female pin header, 2 pins [form="♀ (female)"]
  J44 = female pin header, 2 pins [form="♀ (female)"]
  J45 = female pin header, 2 pins [form="♀ (female)"]
  J46 = female pin header, 2 pins [form="♀ (female)"]
  J47 = female pin header, 2 pins [form="♀ (female)"]
  J48 = female pin header, 2 pins [form="♀ (female)"]
  J49 = female pin header, 2 pins [form="♀ (female)"]
  +_for_buttons2 = female pin header, 1 pin [form="♀ (female)"]
  +_for_buttons3 = female pin header, 1 pin [form="♀ (female)"]
  -_for_LEDs2 = female pin header, 1 pin [form="♀ (female)"]
  -_for_LEDs3 = female pin header, 1 pin [form="♀ (female)"]

nets:
  N1: IC3.pin1, U5.D4, J9.pin1, J13.pin1
  N2: IC3.pin2, J7.pin6
  GND: IC3.pin4, C6.0, U5.GND, C10.-, C11.0, C12.-, C13.0, U6.GND, IC4.0V, Batt_-.pin1, J12.pin2, J14.pin2, Speaker_-3.pin1, R8.Pin_0, R9.Pin_0, R10.Pin_0, R11.Pin_0, R13.Pin_1
  N3: IC3.pin6, J8.pin4
  N4: IC3.pin7, J8.pin1
  N5: IC3.pin11, J8.pin5
  N6: IC3.pin12, U5.D2, J9.pin3, J13.pin3
  N7: IC3.pin13, U5.D3_(PWM), J9.pin2, J13.pin2
  N8: IC3.pin14, J8.pin2
  N9: IC3.pin15, J8.pin3
  N10: IC3.pin16, J8.pin6
  N11: IC3.pin17, J7.pin5
  N12: IC3.pin18, R7.Pin_1
  N13: IC3.pin19, R7.Pin_0, C6.1, U5.VCC, U5.AVCC, U5.AREF, C10.+, U6.output_voltage, IC4.+V, J12.pin1, J14.pin1, +_for_buttons.pin1, R14.Pin_0, R15.Pin_0
  N14: IC3.pin20, J7.pin4
  N15: IC3.pin21, J7.pin1
  N16: IC3.pin22, J7.pin3
  N17: IC3.pin23, J7.pin2
  N18: U5.XLAT1, XTAL3.pin_0, C13.1
  N19: U5.XLAT2, XTAL3.pin_1, C11.1
  N20: U5.D5_(PWM), R12.Pin_1
  N21: U5.D6_(PWM), J16.pin1, R8.Pin_1
  N22: U5.D7, J16.pin2
  N23: U5.D8, R9.Pin_1, J17.pin1
  N24: U5.D9_(PWM), J17.pin2
  N25: U5.D10_(PWM), J18.pin2, R11.Pin_1
  N26: U5.D11_(PWM), J18.pin1
  N27: U5.D12, J19.pin2, R10.Pin_1
  N28: U5.D13, J19.pin1
  N29: U5.A4, IC4.SDA_-_I2C_Data, J12.pin4, J14.pin4, R15.Pin_1
  N30: U5.A5, IC4.SCL_-_I2C_Clock, J12.pin3, J14.pin3, R14.Pin_1
  N31: C12.+, U6.input_voltage
  N32: IC4.X1_-_Crystal, 32_kHz.pin1
  N33: IC4.X2_-_Crystal, Xtal.pin1
  N34: IC4.Vbat_-_Backup_Supply, Batt_+.pin1
  N35: Spkr_+3.pin1, R12.Pin_0
  N36: -_for_LEDs.pin1, R13.Pin_0
  N37: U7.D2, J22.pin3
  N38: U7.D3_(PWM), J22.pin2
  N39: U7.D4, J22.pin1
  N40: U7.VCC, U7.AVCC, U7.AREF, C14.+, R16.Pin_0, R17.Pin_0, U8.output_voltage, C18.1, J24.pin1, +_for_buttons1.pin1
  GND_2: U7.GND, C14.-, C15.0, C16.-, C17.0, R18.Pin_1, R20.Pin_0, R21.Pin_0, R22.Pin_0, R23.Pin_0, U8.GND, C18.0, Speaker_-4.pin1, J24.pin2
  N41: U7.XLAT1, XTAL4.pin_0, C17.1
  N42: U7.XLAT2, XTAL4.pin_1, C15.1
  N43: U7.D5_(PWM), R19.Pin_1
  N44: U7.D6_(PWM), R23.Pin_1, J29.pin1
  N45: U7.D7, J29.pin2
  N46: U7.D8, R22.Pin_1, J28.pin1
  N47: U7.D9_(PWM), J28.pin2
  N48: U7.D10_(PWM), R20.Pin_1, J27.pin2
  N49: U7.D11_(PWM), J27.pin1
  N50: U7.D12, R21.Pin_1, J26.pin2
  N51: U7.D13, J26.pin1
  N52: U7.A4, R16.Pin_1, J24.pin4
  N53: U7.A5, R17.Pin_1, J24.pin3
  N54: IC5.pin1, J23.pin1
  N55: IC5.pin2, J20.pin6
  N56: IC5.pin4, IC6.0V, Batt_-1.pin1, J25.pin2
  N57: IC5.pin6, J21.pin4
  N58: IC5.pin7, J21.pin1
  N59: IC5.pin11, J21.pin5
  N60: IC5.pin12, J23.pin3
  N61: IC5.pin13, J23.pin2
  N62: IC5.pin14, J21.pin2
  N63: IC5.pin15, J21.pin3
  N64: IC5.pin16, J21.pin6
  N65: IC5.pin17, J20.pin5
  N66: IC5.pin18, R24.Pin_1
  N67: IC5.pin19, R24.Pin_0, IC6.+V, J25.pin1
  N68: IC5.pin20, J20.pin4
  N69: IC5.pin21, J20.pin1
  N70: IC5.pin22, J20.pin3
  N71: IC5.pin23, J20.pin2
  N72: C16.+, U8.input_voltage
  N73: R18.Pin_0, -_for_LEDs1.pin1
  N74: R19.Pin_0, Spkr_+4.pin1
  N75: IC6.X1_-_Crystal, 32_kHz1.pin1
  N76: IC6.X2_-_Crystal, Xtal1.pin1
  N77: IC6.Vbat_-_Backup_Supply, Batt_+1.pin1
  N78: IC6.SDA_-_I2C_Data, J25.pin4
  N79: IC6.SCL_-_I2C_Clock, J25.pin3
  N80: U9.D2, J34.pin3
  N81: U9.D3_(PWM), J34.pin2
  N82: U9.D4, J34.pin1
  N83: U9.VCC, U9.AVCC, U9.AREF, C19.+, R25.Pin_0, R27.Pin_0, U11.output_voltage, C27.1, J38.pin1, +_for_buttons2.pin1
  GND_3: U9.GND, C19.-, C22.0, C23.-, C25.0, R29.Pin_1, R33.Pin_0, R35.Pin_0, R37.Pin_0, R39.Pin_0, U11.GND, C27.0, Speaker_-5.pin1, J38.pin2
  N84: U9.XLAT1, XTAL5.pin_0, C25.1
  N85: U9.XLAT2, XTAL5.pin_1, C22.1
  N86: U9.D5_(PWM), R31.Pin_1
  N87: U9.D6_(PWM), R39.Pin_1, J48.pin1
  N88: U9.D7, J48.pin2
  N89: U9.D8, R37.Pin_1, J46.pin1
  N90: U9.D9_(PWM), J46.pin2
  N91: U9.D10_(PWM), R33.Pin_1, J44.pin2
  N92: U9.D11_(PWM), J44.pin1
  N93: U9.D12, R35.Pin_1, J42.pin2
  N94: U9.D13, J42.pin1
  N95: U9.A4, R25.Pin_1, J38.pin4
  N96: U9.A5, R27.Pin_1, J38.pin3
  N97: U10.D2, J35.pin3
  N98: U10.D3_(PWM), J35.pin2
  N99: U10.D4, J35.pin1
  N100: U10.VCC, U10.AVCC, U10.AREF, C20.+, R26.Pin_0, R28.Pin_0, U12.output_voltage, C28.1, J39.pin1, +_for_buttons3.pin1
  GND_4: U10.GND, C20.-, C21.0, C24.-, C26.0, R30.Pin_1, R34.Pin_0, R36.Pin_0, R38.Pin_0, R40.Pin_0, U12.GND, C28.0, Speaker_-6.pin1, J39.pin2
  N101: U10.XLAT1, XTAL6.pin_0, C26.1
  N102: U10.XLAT2, XTAL6.pin_1, C21.1
  N103: U10.D5_(PWM), R32.Pin_1
  N104: U10.D6_(PWM), R40.Pin_1, J49.pin1
  N105: U10.D7, J49.pin2
  N106: U10.D8, R38.Pin_1, J47.pin1
  N107: U10.D9_(PWM), J47.pin2
  N108: U10.D10_(PWM), R34.Pin_1, J45.pin2
  N109: U10.D11_(PWM), J45.pin1
  N110: U10.D12, R36.Pin_1, J43.pin2
  N111: U10.D13, J43.pin1
  N112: U10.A4, R26.Pin_1, J39.pin4
  N113: U10.A5, R28.Pin_1, J39.pin3
  N114: IC7.pin1, J36.pin1
  N115: IC7.pin2, J30.pin6
  N116: IC7.pin4, IC9.0V, Batt_-2.pin1, J40.pin2
  N117: IC7.pin6, J32.pin4
  N118: IC7.pin7, J32.pin1
  N119: IC7.pin11, J32.pin5
  N120: IC7.pin12, J36.pin3
  N121: IC7.pin13, J36.pin2
  N122: IC7.pin14, J32.pin2
  N123: IC7.pin15, J32.pin3
  N124: IC7.pin16, J32.pin6
  N125: IC7.pin17, J30.pin5
  N126: IC7.pin18, R41.Pin_1
  N127: IC7.pin19, R41.Pin_0, IC9.+V, J40.pin1
  N128: IC7.pin20, J30.pin4
  N129: IC7.pin21, J30.pin1
  N130: IC7.pin22, J30.pin3
  N131: IC7.pin23, J30.pin2
  N132: IC8.pin1, J37.pin1
  N133: IC8.pin2, J31.pin6
  N134: IC8.pin4, IC10.0V, Batt_-3.pin1, J41.pin2
  N135: IC8.pin6, J33.pin4
  N136: IC8.pin7, J33.pin1
  N137: IC8.pin11, J33.pin5
  N138: IC8.pin12, J37.pin3
  N139: IC8.pin13, J37.pin2
  N140: IC8.pin14, J33.pin2
  N141: IC8.pin15, J33.pin3
  N142: IC8.pin16, J33.pin6
  N143: IC8.pin17, J31.pin5
  N144: IC8.pin18, R42.Pin_1
  N145: IC8.pin19, R42.Pin_0, IC10.+V, J41.pin1
  N146: IC8.pin20, J31.pin4
  N147: IC8.pin21, J31.pin1
  N148: IC8.pin22, J31.pin3
  N149: IC8.pin23, J31.pin2
  N150: C23.+, U11.input_voltage
  N151: C24.+, U12.input_voltage
  N152: R29.Pin_0, -_for_LEDs2.pin1
  N153: R30.Pin_0, -_for_LEDs3.pin1
  N154: R31.Pin_0, Spkr_+5.pin1
  N155: R32.Pin_0, Spkr_+6.pin1
  N156: IC9.X1_-_Crystal, 32_kHz2.pin1
  N157: IC9.X2_-_Crystal, Xtal2.pin1
  N158: IC9.Vbat_-_Backup_Supply, Batt_+2.pin1
  N159: IC9.SDA_-_I2C_Data, J40.pin4
  N160: IC9.SCL_-_I2C_Clock, J40.pin3
  N161: IC10.X1_-_Crystal, 32_kHz3.pin1
  N162: IC10.X2_-_Crystal, Xtal3.pin1
  N163: IC10.Vbat_-_Backup_Supply, Batt_+3.pin1
  N164: IC10.SDA_-_I2C_Data, J41.pin4
  N165: IC10.SCL_-_I2C_Clock, J41.pin3

notes:
  *
